# Fritzing sketch BlinkingLED (saved by Fritzing 0.9.3b)
breadboards: 1

parts:
  Raspberry_Pi2 = Raspberry Pi B+
  R1 = Resistor [tolerance=±5% resistance=680 package=THT]
  LED1 = LED - 5mm [color="Red (633nm)" package="5 mm [THT]"]

nets:
  N1: Raspberry_Pi2.GPIO3, Raspberry_Pi2.GND, R1.Pin_0
  N2: Raspberry_Pi2.GPIO17, Raspberry_Pi2.GPIO18, LED1.anode
  N3: R1.Pin_1, LED1.cathode
