# Fritzing sketch ButtonLED (saved by Fritzing 0.9.3b)
breadboards: 1

parts:
  Raspberry_Pi1 = Raspberry Pi B+
  S1 = Pushbutton [package="[THT]"]
  R1 = Resistor [tolerance=±5% resistance=680 package=THT]
  LED1 = LED - 5mm [color="Red (633nm)" package="5 mm [THT]"]

nets:
  N1: Raspberry_Pi1.GPIO2, S1.Pin_1, S1.Pin_2
  N2: Raspberry_Pi1.GND, S1.Pin_3, S1.Pin_4, R1.Pin_0
  N3: Raspberry_Pi1.GPIO18, LED1.anode
  N4: R1.Pin_1, LED1.cathode
