# Fritzing sketch Buzzer (saved by Fritzing 0.9.3b)
breadboards: 1

parts:
  Raspberry_Pi1 = Raspberry Pi B+
  J1 = Piezo Speaker

nets:
  N1: Raspberry_Pi1.GND, J1.pin2
  N2: Raspberry_Pi1.GPIO18, J1.pin1

notes:
  Active Buzzer 3V Magnetic Long Continous Beep Tone Alarm Ringer
