# Fritzing sketch DHT11TempSensor (saved by Fritzing 0.9.3b)
breadboards: 1

parts:
  Raspberry_Pi1 = Raspberry Pi B+
  RHT1 = Humidity and Temperature Sensor RHT03 [part_number=DHT11]
  R1 = Resistor [tolerance=±5% resistance=10k package=THT]

nets:
  3V3: Raspberry_Pi1.3v3, RHT1.Vcc, R1.Pin_0
  N1: Raspberry_Pi1.GND, RHT1.GND_2
  N2: Raspberry_Pi1.GPIO18, RHT1.Data-signal, R1.Pin_1

notes:
  This is the DHT11 temp and humidity sensor.
  10K resistor
