# Fritzing sketch PWMRGBLED (saved by Fritzing 0.9.3b)
breadboards: 1

parts:
  Raspberry_Pi1 = Raspberry Pi B+
  R1 = Resistor [tolerance=±5% resistance=680 package=THT]
  Part1 = 16-Channel 12-bit PWM Servo Driver - I2C [part_number=815]
  LED2 = RGB LED (com. cathode, rgb) [package="5 mm [THT]"]
  R2 = Resistor [tolerance=±5% resistance=680 package=THT]
  R3 = Resistor [tolerance=±5% resistance=680 package=THT]

nets:
  3V3: Raspberry_Pi1.3v3, Raspberry_Pi1.GPIO2, Raspberry_Pi1.GPIO3, Raspberry_Pi1.5V, Part1.5.0V, Part1.VCC, Part1.SDA, Part1.SCL
  GND: Raspberry_Pi1.GND, Part1.GND, LED2.common_cathode
  N1: R1.Pin_0, LED2.red_anode
  N2: R1.Pin_1, Part1.PWM0
  N3: Part1.PWM2, R3.Pin_1
  N4: Part1.PWM1, R2.Pin_1
  N5: LED2.green_anode, R2.Pin_0
  N6: LED2.blue_anode, R3.Pin_0

notes:
  PCA9685 16 Channel 12 Bit PWM Servo Driver

custom parts:
  16-Channel 12-bit PWM Servo Driver - I2C: You want to make a cool robot, maybe a hexapod walker, or maybe just a piece of art with a lot of moving parts. Or maybe you want to drive a lot of LEDs with precise PWM output. Using only two pins, control 16 free-running PWM outputs! You can even chain up 62 breakouts to control up to 992 PWM outputs.
