# Fritzing sketch PWMServo (saved by Fritzing 0.9.3b)

parts:
  Raspberry_Pi1 = Raspberry Pi B+
  Part1 = 16-Channel 12-bit PWM Servo Driver - I2C [part_number=815]
  J1 = Basic Servo
  Part2 = Breadboard Power Supply Board SMD

nets:
  VCC: Raspberry_Pi1.3v3, Raspberry_Pi1.GPIO2, Raspberry_Pi1.GPIO3, Raspberry_Pi1.5V, Part1.5.0V, Part1.VCC, Part1.SDA, Part1.SCL, J1.vcc
  GND: Raspberry_Pi1.GND, Part1.GND, J1.gnd, Part2.GND
  N1: Part1.PWRIN, Part2.VCC
  N2: Part1.PWM0, J1.pulse

notes:
  PCA9685 16 Channel 12 Bit PWM Servo Driver
  External 5V power supply
  Tower Pro SG90 Servo

custom parts:
  16-Channel 12-bit PWM Servo Driver - I2C: You want to make a cool robot, maybe a hexapod walker, or maybe just a piece of art with a lot of moving parts. Or maybe you want to drive a lot of LEDs with precise PWM output. Using only two pins, control 16 free-running PWM outputs! You can even chain up 62 breakouts to control up to 992 PWM outputs.
