# Fritzing sketch Photocell (saved by Fritzing 0.9.3b)
breadboards: 1

parts:
  Raspberry_Pi1 = Raspberry Pi B+
  C1 = Electrolytic Capacitor [capacitance=10µF package="100 mil [THT, electrolytic]"]
  R3 = Photocell (LDR) [package=THT]

nets:
  N1: Raspberry_Pi1.3v3, R3.pin_0
  N2: Raspberry_Pi1.GND, C1.-
  N3: Raspberry_Pi1.GPIO18, C1.+, R3.pin_1

notes:
  1uF capacitor
