# Fritzing sketch RGBLED (saved by Fritzing 0.9.3b)
breadboards: 1

parts:
  Raspberry_Pi1 = Raspberry Pi B+
  LED1 = RGB LED (com. cathode, rgb) [package="5 mm [THT]"]
  R1 = Resistor [tolerance=±5% resistance=680 package=THT]
  R2 = Resistor [tolerance=±5% resistance=680 package=THT]
  R3 = Resistor [tolerance=±5% resistance=680 package=THT]

nets:
  N1: Raspberry_Pi1.GPIO17, R3.Pin_0
  N2: Raspberry_Pi1.GPIO27, R1.Pin_0
  N3: Raspberry_Pi1.GPIO18, R2.Pin_0
  N4: LED1.red_anode, R3.Pin_1
  N5: LED1.green_anode, R2.Pin_1
  N6: LED1.blue_anode, R1.Pin_1
