# Fritzing sketch TMP102TempSensor (saved by Fritzing 0.9.3b)
breadboards: 1

parts:
  Raspberry_Pi1 = Raspberry Pi B+
  Part1 = Digital Temperature Sensor Breakout - TMP102

nets:
  N1: Raspberry_Pi1.3v3, Part1.V+
  N2: Raspberry_Pi1.GPIO2, Part1.SDA
  N3: Raspberry_Pi1.GPIO3, Part1.SCL
  GND: Raspberry_Pi1.GND, Part1.GND, Part1.ADD0

notes:
  The new TMP102 model, SEN-11931, is used in the actual jpg images. The TMP102 here works, but is just an earlier version.
